# Fritzing sketch carrito (saved by Fritzing 0.9.3b)
breadboards: 1

parts:
  Componente3 = NRF24L01+ Breakout Board
  IC1 = SHIFT REGISTER [package=dil16]
  JP1 = Header 2 [package=screwterminal-3.5mm-2_lock]
  Componente2 = Arduino Pro Mini (3.3V)
  M1 = Stepper Motor - Unipolar
  Q4 = Basic FET N-Channel [package="TO220 [THT]"]
  R1 = Resistor [tolerance=±5% resistance=220 package=THT]
  R2 = Resistor [tolerance=±5% resistance=220 package=THT]
  R3 = Resistor [tolerance=±5% resistance=220 package=THT]
  R4 = Resistor [tolerance=±5% resistance=220 package=THT]
  Q5 = Basic FET N-Channel [package="TO220 [THT]"]
  Q6 = Basic FET N-Channel [package="TO220 [THT]"]
  Q7 = Basic FET N-Channel [package="TO220 [THT]"]
  Q8 = pnp-Powertransistor [package="TO220 [THT]"]
  Q9 = TRANSISTOR_PNP [package=to-92]
  R5 = Resistor [tolerance=±20% resistance=510 package=THT]
  R6 = Resistor [tolerance=±20% resistance=0.51 package=THT]
  S1 = Momentary Switch [package=ksa_sealed_tac_switch]
  U1 = HALL-EFFECT [package=sc70]
  R8 = Resistor [tolerance=±20% resistance=10k package=THT]
  R7 = Resistor [tolerance=±20% resistance=10k package=THT]
  S2 = Momentary Switch [package=ksa_sealed_tac_switch]
  JP2 = Header 4 [package=screwterminal-3.5mm-4_lock]

nets:
  GND: Componente3.GND, IC1.GND, IC1.G, JP1.1, Componente2.GND, Q4.source, Q5.source, Q6.source, Q7.source, R5.Pin_0, U1.GND, R8.Pin_0, S2.2, JP2.3
  VCC: Componente3.VCC, IC1.SCL, IC1.VCC, Componente2.VCC, S1.4, U1.VCC, R7.Pin_1
  N1: Componente3.CE, Componente2.D9
  N2: Componente3.CS, Componente2.D10
  N3: Componente3.SCK, IC1.SCK, Componente2.SCK
  N4: Componente3.MOSI, IC1.SER, Componente2.MOSI
  N5: Componente3.MISO, Componente2.MISO
  N6: IC1.QE, R4.Pin_1
  N7: IC1.QF, R2.Pin_1
  N8: IC1.QG, R3.Pin_1
  N9: IC1.QH, R1.Pin_1
  N10: IC1.RCK, Componente2.D8
  N11: JP1.2, Componente2.RAW, Q9.E, R6.Pin_1, JP2.4
  N12: Componente2.D6, JP2.1
  N13: Componente2.D5, JP2.2
  N14: Componente2.D4, U1.OUT
  N15: M1.A, Q7.drain
  N16: M1.COMMON_1, M1.COMMON_2, Q8.collector
  N17: M1.C, Q6.drain
  N18: M1.B, Q5.drain
  N19: M1.D, Q4.drain
  N20: Q4.gate, R1.Pin_0
  N21: R2.Pin_0, Q6.gate
  N22: R3.Pin_0, Q5.gate
  N23: R4.Pin_0, Q7.gate
  N24: Q8.base, Q9.C, R5.Pin_1
  N25: Q8.emitter, Q9.B, R6.Pin_0
  N26: S1.2, R8.Pin_1, R7.Pin_0, S2.4

notes:
  6.0v to 8.4V From a 2P2S Lithium Ion Battery with a proper BMS
  This is a basic Current Source to feed the Stepper motor, in this case 1.2 Amps aprox.
  A Heat Sink is mandatory
  Power Transistor is 2SA1568
  Lower Power one is 2N3906
  This is the motor that turns the front wheels.
  It's a NEMA17 like 3V@1.2A Unipolar one.
  Brand is MINEBEA (MNB)
  Al 4 N-channel MosFET are PL06N03 SMD ones
  nRF24L01 Module
  Two momentary limit switch (the positive feed is the one at the right, the negative feeded is at left)
  One Hall sensor to sign we are facing ahead (it's pulled down when magnet is on position, high the rest of the time)
  H-bridge connector + Speed control.
  The function is as follow:
  * Pin 5 controls the car movement direction (low forward, hig reverse)
  * Pin 6 is a PWM control of the speed of the movement (with a P-channel MosFET) 0 is no movement and 255 is full power, Positive going PWM.
  Carrito: A remote controlled car from parts in my junkbox
  =================================================
  Author: Pavel Milanes (CO7WT)
  E-mail: pavelmc@gmail.com
  Web: https://github.com/pavelmc/carrito
